// Logisim project Guia_0501.circ as structural Verilog: 1 circuit, main circuit main
module main (
  input  X,
  input  Y,
  input  X_2,
  input  Y_2,
  output S1,
  output S1_2
);

  wire not_1_out, not_2_out;

  not not_1 (not_1_out, X_2);
  not not_2 (not_2_out, Y_2);
  nor nor_1 (S1, X, Y);
  and and_1 (S1_2, not_1_out, not_2_out);

  // Notes on the sheet:
  //   NOR GATE
  //   (~A  ^ ~B)
endmodule
