// Logisim project Guia_0502.circ as structural Verilog: 1 circuit, main circuit main
module main (
  input  x,
  input  y,
  input  x_2,
  input  y_2,
  output s1,
  output s1_2
);

  wire nand_1_out, not_1_out;

  nand nand_1 (nand_1_out, y, y);
  not not_1 (not_1_out, x_2);
  nand nand_2 (s1, x, nand_1_out);
  or or_1 (s1_2, not_1_out, y_2);

  // Notes on the sheet:
  //   (~A + B)
  //   Expressao usando NAND's
  //   Expressao padrão
endmodule
