// Logisim project Guia_0503.circ as structural Verilog: 1 circuit, main circuit main
module main (
  input  x,
  input  y,
  input  x_2,
  input  y_2,
  output s1,
  output s1_2
);

  wire nor_1_out, nor_3_out, not_1_out;

  not not_1 (not_1_out, y_2);
  nor nor_1 (nor_1_out, y, y);
  nor nor_2 (s1, nor_3_out, nor_3_out);
  nor nor_3 (nor_3_out, x, nor_1_out);
  or or_1 (s1_2, x_2, not_1_out);

  // Notes on the sheet:
  //   (A + ~B)
  //   Expressao usando NOR's
  //   Expressao padrão
endmodule
