// Logisim project Guia_0504.circ as structural Verilog: 1 circuit, main circuit main
module main (
  input  in_1,
  input  in_2,
  input  x,
  input  y,
  output out_5,
  output s1
);

  wire nand_1_out, nand_2_out, not_1_out;

  nand nand_1 (nand_1_out, in_1, in_1);
  not not_1 (not_1_out, x);
  nand nand_2 (nand_2_out, nand_1_out, in_2);
  and and_1 (s1, not_1_out, y);
  nand nand_3 (out_5, nand_2_out, nand_2_out);

  // Notes on the sheet:
  //   (~A * B)
  //   Expressao usando NAND's
  //   Expressao padrão
endmodule
