// Logisim project Guia_0505.circ as structural Verilog: 1 circuit, main circuit main
module main (
  input  x,
  input  y,
  input  x_2,
  input  y_2,
  output s1,
  output s1_2
);

  wire nor_1_out, nor_2_out, nor_3_out;

  nor nor_1 (nor_1_out, x, nor_2_out);
  nor nor_2 (nor_2_out, x, y);
  nor nor_3 (nor_3_out, nor_2_out, y);
  nor nor_4 (s1, nor_1_out, nor_3_out);
  xnor xnor_1 (s1_2, x_2, y_2);

  // Notes on the sheet:
  //   (~(A * B) = A xnor B)
  //   Expressao usando NOR's
  //   Expressao padrão
endmodule
