// Logisim project Guia_0506.circ as structural Verilog: 1 circuit, main circuit main
module main (
  input  x,
  input  y,
  input  x_2,
  input  y_2,
  output s1,
  output s1_2
);

  wire nand_1_out, nand_2_out, nand_3_out;

  nand nand_1 (nand_1_out, x, y);
  nand nand_2 (nand_2_out, x, nand_1_out);
  nand nand_3 (nand_3_out, nand_1_out, y);
  xor xor_1 (s1_2, x_2, y_2);
  nand nand_4 (s1, nand_2_out, nand_3_out);

  // Notes on the sheet:
  //   (A * B = A xor B)
  //   Expressao usando NAND's
  //   Expressao padrão
endmodule
