// Logisim project GUIA_0601a.circ as structural Verilog
module XZ_ZY (
  input  X,
  input  Y,
  input  Z,
  output S
);

  wire nand_1_out, nand_2_out, nand_3_out;

  nand nand_1 (nand_1_out, Y, Y);
  nand nand_2 (nand_2_out, nand_1_out, Z);
  nand nand_3 (nand_3_out, X, Z);
  nand nand_4 (S, nand_2_out, nand_3_out);
endmodule
