// Logisim project Guia_0601c.circ as structural Verilog
module z_y_z_x_xy (
  input  x,
  input  y,
  input  z,
  output s
);

  wire nand_1_out, nand_2_out, nand_3_out, nand_4_out, nand_5_out;

  nand nand_1 (nand_1_out, z, z);
  nand nand_2 (nand_2_out, z, z);
  nand nand_3 (nand_3_out, y, nand_1_out);
  nand nand_4 (nand_4_out, x, nand_2_out);
  nand nand_5 (nand_5_out, x, y);
  nand nand_6 (s, nand_3_out, nand_4_out, nand_5_out);
endmodule
