// Logisim project Guia_0601d.circ as structural Verilog
module x_z_z_y (
  input  x,
  input  y,
  input  z,
  output s
);

  wire nand_1_out, nand_2_out, nand_3_out, nand_4_out;

  nand nand_1 (nand_1_out, x, x);
  nand nand_2 (nand_2_out, z, z);
  nand nand_3 (nand_3_out, nand_1_out, z);
  nand nand_4 (nand_4_out, y, nand_2_out);
  nand nand_5 (s, nand_3_out, nand_4_out);
endmodule
