// Logisim project Guia_0602a.circ as structural Verilog
module x__z__x__y (
  input  X,
  input  Y,
  input  Z,
  output S
);

  wire nand_1_out, nand_2_out, nand_3_out, nand_4_out;

  nand nand_1 (nand_1_out, Z, Z);
  nand nand_2 (nand_2_out, X, nand_1_out);
  nand nand_3 (nand_3_out, X, Y);
  nand nand_4 (nand_4_out, nand_2_out, nand_3_out);
  nand nand_5 (S, nand_4_out, nand_4_out);
endmodule
