// Logisim project Guia_0602b.circ as structural Verilog
module y_z___x__y__z (
  input  x,
  input  y,
  input  z,
  output s
);

  wire nand_1_out, nand_2_out, nand_3_out, nand_4_out, nand_5_out;

  nand nand_1 (nand_1_out, y, y);
  nand nand_2 (nand_2_out, z, z);
  nand nand_3 (nand_3_out, nand_1_out, z);
  nand nand_4 (nand_4_out, x, y, nand_2_out);
  nand nand_5 (nand_5_out, nand_3_out, nand_4_out);
  nand nand_6 (s, nand_5_out, nand_5_out);
endmodule
