// Logisim project Guia_0603d.circ as structural Verilog
module _3d (
  input  x,
  input  y,
  input  w,
  input  z,
  output s
);

  wire nand_1_out, nand_2_out, nand_3_out, nand_4_out, nand_5_out, nand_6_out, nand_7_out, nand_8_out,
       nand_9_out, nand_10_out, nand_11_out, nand_12_out;

  nand nand_1 (nand_1_out, y, y);
  nand nand_2 (nand_2_out, z, z);
  nand nand_3 (nand_3_out, x, x);
  nand nand_4 (nand_4_out, w, w);
  nand nand_5 (nand_5_out, x, x);
  nand nand_6 (nand_6_out, w, w);
  nand nand_7 (nand_7_out, z, z);
  nand nand_8 (nand_8_out, nand_1_out, w, nand_2_out);
  nand nand_9 (nand_9_out, nand_3_out, y, nand_4_out);
  nand nand_10 (nand_10_out, nand_5_out, y, z);
  nand nand_11 (nand_11_out, y, nand_6_out, z);
  nand nand_12 (nand_12_out, x, w, nand_7_out);
  nand nand_13 (s, nand_8_out, nand_9_out, nand_10_out, nand_11_out, nand_12_out);
endmodule
