// Logisim project Guia_0603e.circ as structural Verilog
module _3e (
  input  x,
  input  y,
  input  w,
  input  z,
  output s
);

  wire nand_1_out, nand_2_out, nand_3_out, nand_4_out;

  nand nand_1 (nand_1_out, y, y);
  nand nand_2 (nand_2_out, w, w);
  nand nand_3 (nand_3_out, nand_1_out, nand_2_out);
  nand nand_4 (nand_4_out, w, z);
  nand nand_5 (s, nand_3_out, nand_4_out);
endmodule
