// Logisim project Guia_0604a.circ as structural Verilog
module _4a (
  input  x,
  input  y,
  input  w,
  input  z,
  output s
);

  wire nand_1_out, nand_2_out, nand_3_out, nand_4_out, nand_5_out, nand_6_out, nand_7_out, nand_8_out,
       nand_9_out;

  nand nand_1 (nand_1_out, x, x);
  nand nand_2 (nand_2_out, y, y);
  nand nand_3 (nand_3_out, z, z);
  nand nand_4 (nand_4_out, x, x);
  nand nand_5 (nand_5_out, w, w);
  nand nand_6 (nand_6_out, nand_1_out, nand_2_out, w, nand_3_out);
  nand nand_7 (nand_7_out, nand_4_out, y, z);
  nand nand_8 (nand_8_out, y, nand_5_out, z);
  nand nand_9 (nand_9_out, nand_6_out, nand_7_out, nand_8_out);
  nand nand_10 (s, nand_9_out, nand_9_out);
endmodule
