// Logisim project Guia_0604b.circ as structural Verilog
module _4b (
  input  x,
  input  y,
  input  w,
  input  z,
  output s
);

  wire nand_1_out, nand_2_out, nand_3_out, nand_4_out, nand_5_out, nand_6_out, nand_7_out, nand_8_out;

  nand nand_1 (nand_1_out, w, w);
  nand nand_2 (nand_2_out, z, z);
  nand nand_3 (nand_3_out, y, y);
  nand nand_4 (nand_4_out, w, w);
  nand nand_5 (nand_5_out, y, nand_1_out, nand_2_out);
  nand nand_6 (nand_6_out, x, nand_3_out, nand_4_out);
  nand nand_7 (nand_7_out, x, y, w, z);
  nand nand_8 (nand_8_out, nand_5_out, nand_6_out, nand_7_out);
  nand nand_9 (s, nand_8_out, nand_8_out);
endmodule
