// Logisim project Guia_0604c.circ as structural Verilog
module _4c (
  input  x,
  input  y,
  input  w,
  input  z,
  output s
);

  wire nand_1_out, nand_2_out, nand_3_out, nand_4_out, nand_5_out, nand_6_out, nand_7_out, nand_8_out,
       nand_9_out, nand_10_out, nand_11_out;

  nand nand_1 (nand_1_out, x, x);
  nand nand_2 (nand_2_out, w, w);
  nand nand_3 (nand_3_out, z, z);
  nand nand_4 (nand_4_out, y, y);
  nand nand_5 (nand_5_out, w, w);
  nand nand_6 (nand_6_out, z, z);
  nand nand_7 (nand_7_out, nand_1_out, y, nand_2_out, nand_3_out);
  nand nand_8 (nand_8_out, x, nand_4_out, nand_5_out, nand_6_out);
  nand nand_9 (nand_9_out, x, w, z);
  nand nand_10 (nand_10_out, x, y, z);
  nand nand_11 (nand_11_out, nand_7_out, nand_8_out, nand_9_out, nand_10_out);
  nand nand_12 (s, nand_11_out, nand_11_out);
endmodule
