// Logisim project Guia_0604d.circ as structural Verilog
module _4d (
  input  x,
  input  y,
  input  w,
  input  z,
  output s
);

  wire nand_1_out, nand_2_out, nand_3_out, nand_4_out, nand_5_out, nand_6_out, nand_7_out;

  nand nand_1 (nand_1_out, x, x);
  nand nand_2 (nand_2_out, y, y);
  nand nand_3 (nand_3_out, w, w);
  nand nand_4 (nand_4_out, nand_1_out, nand_2_out, z);
  nand nand_5 (nand_5_out, y, nand_3_out, z);
  nand nand_6 (nand_6_out, x, y, w);
  nand nand_7 (nand_7_out, nand_4_out, nand_5_out, nand_6_out);
  nand nand_8 (s, nand_7_out, nand_7_out);
endmodule
