// Logisim project Guia_0604e.circ as structural Verilog
module _4e (
  input  x,
  input  y,
  input  w,
  input  z,
  output s
);

  wire nand_1_out, nand_2_out, nand_3_out, nand_4_out, nand_5_out, nand_6_out, nand_7_out;

  nand nand_1 (nand_1_out, x, x);
  nand nand_2 (nand_2_out, w, w);
  nand nand_3 (nand_3_out, z, z);
  nand nand_4 (nand_4_out, nand_1_out, w, z);
  nand nand_5 (nand_5_out, y, nand_2_out, z);
  nand nand_6 (nand_6_out, y, w, nand_3_out);
  nand nand_7 (nand_7_out, nand_4_out, nand_5_out, nand_6_out);
  nand nand_8 (s, nand_7_out, nand_7_out);
endmodule
