// Logisim project Guia_0701.circ as structural Verilog: 1 circuit, main circuit main
module main (
  input  X,
  input  Y,
  input  Key,
  output out_4
);

  wire and_1_out, and_2_out, and_3_out, nand_1_out, not_1_out;

  and and_1 (and_1_out, Y, X);
  nand nand_1 (nand_1_out, Y, X);
  and and_2 (and_2_out, and_1_out, not_1_out);
  not not_1 (not_1_out, Key);
  and and_3 (and_3_out, Key, nand_1_out);
  or or_1 (out_4, and_2_out, and_3_out);

  // Notes on the sheet:
  //   MUX 2x1
endmodule
