// Logisim project Guia_0702.circ as structural Verilog: 1 circuit, main circuit main
module main (
  input  X,
  input  Y,
  input  Key,
  output out_4
);

  wire and_1_out, and_2_out, nor_1_out, not_1_out, or_1_out;

  or or_1 (or_1_out, Y, X);
  nor nor_1 (nor_1_out, Y, X);
  and and_1 (and_1_out, or_1_out, not_1_out);
  not not_1 (not_1_out, Key);
  and and_2 (and_2_out, Key, nor_1_out);
  or or_2 (out_4, and_1_out, and_2_out);

  // Notes on the sheet:
  //   MUX 2x1
endmodule
