// Logisim project Guia_0704.circ as structural Verilog: 1 circuit, main circuit main
module main (
  input  X,
  input  Y,
  input  A,
  input  B,
  output out_5
);

  wire and_1_out, and_2_out, and_3_out, and_4_out, nor_1_out, not_1_out, not_2_out, not_3_out, not_4_out,
       or_1_out, xnor_1_out, xor_1_out;

  xor xor_1 (xor_1_out, Y, X);
  xnor xnor_1 (xnor_1_out, Y, X);
  or or_1 (or_1_out, Y, X);
  nor nor_1 (nor_1_out, Y, X);
  not not_1 (not_1_out, A);
  not not_2 (not_2_out, B);
  not not_3 (not_3_out, A);
  not not_4 (not_4_out, B);
  and and_1 (and_1_out, xor_1_out, not_1_out, not_2_out);
  and and_2 (and_2_out, xnor_1_out, not_3_out, B);
  and and_3 (and_3_out, or_1_out, A, not_4_out);
  and and_4 (and_4_out, A, nor_1_out, B);
  or or_2 (out_5, and_1_out, and_2_out, and_3_out, and_4_out);

  // Notes on the sheet:
  //   MUX 4x1
endmodule
