// Logisim project Guia_0705.circ as structural Verilog: 1 circuit, main circuit main
module main (
  input  X,
  input  Y,
  input  A,
  input  B,
  input  C,
  output out_6
);

  wire and_1_out, and_2_out, and_3_out, and_4_out, and_5_out, and_6_out, and_7_out, and_8_out, and_9_out,
       nand_1_out, nor_1_out, not_1_out, not_2_out, not_3_out, not_4_out, not_5_out, or_1_out, xnor_1_out,
       xor_1_out;

  not not_1 (not_1_out, Y);
  not not_2 (not_2_out, X);
  and and_1 (and_1_out, Y, X);
  nand nand_1 (nand_1_out, Y, X);
  xor xor_1 (xor_1_out, Y, X);
  xnor xnor_1 (xnor_1_out, Y, X);
  or or_1 (or_1_out, Y, X);
  nor nor_1 (nor_1_out, Y, X);
  not not_3 (not_3_out, A);
  not not_4 (not_4_out, B);
  not not_5 (not_5_out, C);
  and and_2 (and_2_out, not_1_out, not_3_out, not_4_out, not_5_out);
  and and_3 (and_3_out, not_2_out, not_3_out, not_4_out, C);
  and and_4 (and_4_out, and_1_out, not_3_out, B, not_5_out);
  and and_5 (and_5_out, nand_1_out, not_3_out, B, C);
  and and_6 (and_6_out, xor_1_out, A, not_4_out, not_5_out);
  and and_7 (and_7_out, xnor_1_out, A, not_4_out, C);
  and and_8 (and_8_out, or_1_out, A, B, not_5_out);
  and and_9 (and_9_out, nor_1_out, A, B, C);
  or or_2 (out_6, and_2_out, and_3_out, and_4_out, and_5_out, and_6_out, and_7_out, and_8_out, and_9_out);

  // Notes on the sheet:
  //   MUX 8x1
endmodule
